// Logisim project 1_bit_adder.circ as structural Verilog: 1 circuit, main circuit main
module main (
  input  in_1,
  input  in_2,
  input  in_3,
  input  in_4,
  input  in_5,
  input  in_6,
  input  in_7,
  input  in_8,
  input  in_9,
  output Sum,
  output out_11,
  output out_12,
  output Carry,
  output out_14,
  output out_15
);

  wire and_1_out, and_2_out, and_3_out, and_4_out, and_5_out, and_6_out, and_7_out, not_1_out, or_1_out,
       xor_1_out, xor_2_out, xor_5_out;

  xor xor_1 (xor_1_out, in_1, in_3);
  and and_1 (and_1_out, in_1, in_3);
  and and_2 (and_2_out, in_3, in_5);
  and and_3 (and_3_out, in_1, in_5);
  xor xor_2 (xor_2_out, in_7, in_8);
  or or_1 (or_1_out, and_1_out, and_2_out);
  and and_4 (and_4_out, in_7, in_8);
  and and_5 (and_5_out, xor_2_out, in_9);
  xor xor_3 (Sum, xor_1_out, in_5);
  or or_2 (Carry, or_1_out, and_3_out);
  xor xor_4 (out_14, xor_2_out, in_9);
  or or_3 (out_15, and_4_out, and_5_out);
  xor xor_5 (xor_5_out, in_2, in_4);
  not not_1 (not_1_out, xor_5_out);
  and and_6 (and_6_out, not_1_out, in_4);
  and and_7 (and_7_out, xor_5_out, in_6);
  xor xor_6 (out_11, xor_5_out, in_6);
  or or_4 (out_12, and_6_out, and_7_out);

  // Notes on the sheet:
  //   1 bit adder v1
  //   1 bit adder v3
  //   1 bit adder v2
endmodule
